# Fritzing sketch wiring-fritzing (saved by Fritzing 0.9.3b)
breadboards: 1

parts:
  Bauteil1 = Arduino Uno (Rev3)
  J1 = Basic Servo
  J2 = Basic Servo
  U1 = POT [package=pot_mammoth]
  U2 = POT [package=pot_mammoth]

nets:
  N1: Bauteil1.A1, U1.A
  N2: Bauteil1.A2, U2.A
  N3: Bauteil1.D9_PWM, J2.pulse
  N4: Bauteil1.D10_PWM/SS, J1.pulse
  VCC: Bauteil1.5V, J1.vcc, J2.vcc, U1.S, U2.S
  GND: Bauteil1.GND, J1.gnd, J2.gnd, U1.E, U2.E
